# Fritzing sketch AIncrivelMaquinaDeBolhas (saved by Fritzing 0.9.2b)
breadboards: 1

parts:
  Componente1 = Arduino Uno (Rev3)
  S1 = Pushbutton [package="[THT]"]
  J1 = Basic Servo
  J2 = Basic Servo
  U1 = RELAY [package=relay-jzc]
  M1 = DC Motor
  VCC1 = Battery block 9V

nets:
  N1: Componente1.D13/SCK, S1.Pin_1, S1.Pin_2
  N2: Componente1.D4, J1.pulse
  N3: Componente1.D6_PWM, J2.pulse
  N4: Componente1.D7, U1.NO
  VCC: Componente1.5V, J1.vcc, J2.vcc, U1.COIL2
  GND: Componente1.GND, S1.Pin_3, S1.Pin_4, J1.gnd, J2.gnd, U1.NC, M1.pin_2, VCC1.-
  N5: Componente1.VIN, U1.COIL1, VCC1.+
  N6: U1.MAIN, M1.pin_1
